// Logisim project 171044079_CSE433_Project1.circ as structural Verilog: 4 circuits, main circuit main
module main (
  input  go,
  input  [7:0] n,
  input  [15:0] num,
  output [15:0] res
);

  wire clock_1_out, control_unit_1_ldcount, control_unit_1_ldnum, control_unit_1_ldnum1,
       control_unit_1_ldnum2, control_unit_1_ldresult, control_unit_1_ldsize, control_unit_1_scount,
       control_unit_1_snum1, control_unit_1_snum2, control_unit_1_sresult, control_unit_1_strnum,
       datapath_1_a, datapath_1_b, datapath_1_c, datapath_1_d, datapath_1_e, datapath_1_f, datapath_1_g,
       datapath_1_h;

  control_unit control_unit_1 (
    .snum1(control_unit_1_snum1), .ldnum1(control_unit_1_ldnum1), .snum2(control_unit_1_snum2),
    .ldnum2(control_unit_1_ldnum2), .scount(control_unit_1_scount), .ldcount(control_unit_1_ldcount),
    .ldsize(control_unit_1_ldsize), .sresult(control_unit_1_sresult), .ldresult(control_unit_1_ldresult),
    .ldnum(control_unit_1_ldnum), .strnum(control_unit_1_strnum), .go(go), .a(datapath_1_a),
    .b(datapath_1_b), .c(datapath_1_c), .d(datapath_1_d), .e(datapath_1_e), .f(datapath_1_f),
    .g(datapath_1_g), .h(datapath_1_h), .clk(clock_1_out));
  Clock clock_1 (.out(clock_1_out));
  datapath datapath_1 (
    .num(num), .n(n), .snum1(control_unit_1_snum1), .snum2(control_unit_1_snum2),
    .scount(control_unit_1_scount), .sresult(control_unit_1_sresult), .strnum(control_unit_1_strnum),
    .ldnum1(control_unit_1_ldnum1), .ldnum2(control_unit_1_ldnum2), .ldcount(control_unit_1_ldcount),
    .ldsize(control_unit_1_ldsize), .ldresult(control_unit_1_ldresult), .ldnum(control_unit_1_ldnum),
    .clk(clock_1_out), .a(datapath_1_a), .b(datapath_1_b), .c(datapath_1_c), .d(datapath_1_d),
    .e(datapath_1_e), .f(datapath_1_f), .g(datapath_1_g), .h(datapath_1_h), .result(res));
endmodule

module states (
  input  P3,
  input  P2,
  input  P1,
  input  P0,
  output S0,
  output S1,
  output S2,
  output S3,
  output S4,
  output S5,
  output S6,
  output S7,
  output S8,
  output S9,
  output S10,
  output S11,
  output S12,
  output S13
);

  and and_1 (S0, ~P3, ~P2, ~P1, ~P0);  // AND_Gate
  and and_2 (S1, ~P3, ~P2, ~P1, P0);  // AND_Gate
  and and_3 (S2, ~P3, ~P2, P1, ~P0);  // AND_Gate
  and and_4 (S3, ~P3, ~P2, P1, P0);  // AND_Gate
  and and_5 (S4, ~P3, P2, ~P1, ~P0);  // AND_Gate
  and and_6 (S5, ~P3, P2, ~P1, P0);  // AND_Gate
  and and_7 (S6, ~P3, P2, P1, ~P0);  // AND_Gate
  and and_8 (S7, ~P3, P2, P1, P0);  // AND_Gate
  and and_9 (S8, P3, ~P2, ~P1, ~P0);  // AND_Gate
  and and_10 (S9, P3, ~P2, ~P1, P0);  // AND_Gate
  and and_11 (S10, P3, ~P2, P1, ~P0);  // AND_Gate
  and and_12 (S11, P3, ~P2, P1, P0);  // AND_Gate
  and and_13 (S12, P3, P2, ~P1, ~P0);  // AND_Gate
  and and_14 (S13, P3, P2, ~P1, P0);  // AND_Gate
endmodule

module control_unit (
  input  go,
  input  a,
  input  b,
  input  c,
  input  d,
  input  e,
  input  f,
  input  g,
  input  h,
  input  clk,
  output snum1,
  output ldnum1,
  output snum2,
  output ldnum2,
  output scount,
  output ldcount,
  output ldsize,
  output sresult,
  output ldresult,
  output ldnum,
  output strnum
);

  wire and_1_out, and_2_out, and_3_out, and_4_out, and_5_out, and_6_out, and_7_out, and_8_out, and_9_out,
       and_10_out, d_ff_1_q, d_ff_2_q, d_ff_3_q, d_ff_4_q, not_1_out, not_2_out, not_3_out, not_4_out,
       not_5_out, not_6_out, not_7_out, not_8_out, or_7_out, or_8_out, or_9_out, or_10_out, states_1_s0,
       states_1_s2, states_1_s4, states_1_s5, states_1_s6, states_1_s7, states_1_s8, states_1_s9,
       states_1_s10;

  states states_1 (
    .P3(d_ff_1_q), .P2(d_ff_2_q), .P1(d_ff_3_q), .P0(d_ff_4_q), .S0(states_1_s0), .S1(ldsize),
    .S2(states_1_s2), .S3(strnum), .S4(states_1_s4), .S5(states_1_s5), .S6(states_1_s6), .S7(states_1_s7),
    .S8(states_1_s8), .S9(states_1_s9), .S10(states_1_s10), .S11(snum2), .S12(snum1), .S13(sresult));
  or or_1 (ldcount, scount, ldsize, states_1_s4);
  or or_2 (ldnum1, snum1, states_1_s8);
  or or_3 (ldnum2, states_1_s8, snum2);
  or or_4 (scount, states_1_s8, states_1_s7, strnum);
  or or_5 (ldresult, sresult, states_1_s7);
  or or_6 (ldnum, states_1_s8, states_1_s7);
  not not_1 (not_1_out, a);
  not not_2 (not_2_out, b);
  not not_3 (not_3_out, c);
  not not_4 (not_4_out, d);
  not not_5 (not_5_out, e);
  not not_6 (not_6_out, f);
  not not_7 (not_7_out, g);
  not not_8 (not_8_out, h);
  and and_1 (and_1_out, d, not_3_out, states_1_s6);
  and and_2 (and_2_out, states_1_s9, e, not_6_out);
  and and_3 (and_3_out, states_1_s9, not_5_out, f);
  and and_4 (and_4_out, states_1_s10, g, not_8_out);
  and and_5 (and_5_out, states_1_s10, not_7_out, h);
  and and_6 (and_6_out, states_1_s2, not_1_out, b);
  and and_7 (and_7_out, states_1_s5, a, not_2_out);
  and and_8 (and_8_out, states_1_s6, c, not_4_out);
  and and_9 (and_9_out, states_1_s2, a, not_2_out);
  and and_10 (and_10_out, states_1_s0, go);
  or or_7 (or_7_out, and_1_out, states_1_s8, and_2_out, and_3_out, and_4_out, and_5_out, snum2, snum1);
  or or_8 (or_8_out, and_6_out, states_1_s4, and_7_out, and_8_out, states_1_s7, and_3_out, and_5_out, sresult);
  or or_9 (or_9_out, ldsize, and_9_out, strnum, and_7_out, and_8_out, and_2_out, and_4_out);
  or or_10 (or_10_out, and_10_out, and_9_out, states_1_s4, and_8_out, states_1_s7, states_1_s8, and_4_out, and_3_out, snum2, snum1, sresult);
  D_Flip_Flop d_ff_1 (.clk(clk), .D(or_7_out), .Q(d_ff_1_q));  // open: Qn, preset, en, reset
  D_Flip_Flop d_ff_2 (.clk(clk), .D(or_8_out), .Q(d_ff_2_q));  // open: Qn, preset, en, reset
  D_Flip_Flop d_ff_3 (.clk(clk), .D(or_9_out), .Q(d_ff_3_q));  // open: Qn, preset, en, reset
  D_Flip_Flop d_ff_4 (.clk(clk), .D(or_10_out), .Q(d_ff_4_q));  // open: Qn, preset, en, reset
endmodule

module datapath (
  input  [15:0] num,
  input  strnum,
  input  ldnum,
  input  snum1,
  input  ldnum1,
  input  snum2,
  input  ldnum2,
  input  scount,
  input  ldcount,
  input  [7:0] n,
  input  ldsize,
  input  sresult,
  input  ldresult,
  input  clk,
  output a,
  output b,
  output c,
  output d,
  output e,
  output f,
  output g,
  output h,
  output [15:0] result
);

  wire comparator_1_gt, comparator_2_eq, comparator_2_lt, comparator_3_gt, comparator_3_lt;
  wire [7:0] adder_1_out, multiplexer_3_out, register_3_q, register_4_q, subtractor_1_out;
  wire [15:0] multiplexer_1_out, multiplexer_2_out, multiplexer_4_out, ram_1_data, register_1_q,
       register_2_q, subtractor_2_out, subtractor_3_out;

  Subtractor subtractor_1 (.a(register_3_q), .b(8'h1), .out(subtractor_1_out));  // open: bin, bout
  Multiplexer #(.width(16), .enable("false")) multiplexer_1 (
    .in0(result), .in1(subtractor_2_out), .out(multiplexer_1_out), .sel(snum1));
  Multiplexer #(.width(16), .enable("false")) multiplexer_2 (
    .in0(ram_1_data), .in1(subtractor_3_out), .out(multiplexer_2_out), .sel(snum2));
  Multiplexer #(.width(8), .enable("false")) multiplexer_3 (
    .in0({8{1'b0}}), .in1(adder_1_out), .out(multiplexer_3_out), .sel(scount));
  Multiplexer #(.width(16), .enable("false")) multiplexer_4 (
    .in0(ram_1_data), .in1(register_1_q), .out(multiplexer_4_out), .sel(sresult));
  Register #(.width(16)) register_1 (.D(multiplexer_1_out), .en(ldnum1), .Q(register_1_q), .clk(clk));  // open: clr
  Register #(.width(16)) register_2 (.D(multiplexer_2_out), .en(ldnum2), .Q(register_2_q), .clk(clk));  // open: clr
  Register register_3 (.D(multiplexer_3_out), .en(ldcount), .Q(register_3_q), .clk(clk));  // open: clr
  Register register_4 (.D(n), .en(ldsize), .Q(register_4_q), .clk(clk));  // open: clr
  Register #(.width(16)) register_5 (.D(multiplexer_4_out), .en(ldresult), .Q(result), .clk(clk));  // open: clr
  RAM #(.dataWidth(16), .bus("separate")) ram_1 (
    .addr(subtractor_1_out), .din(num), .data(ram_1_data), .str(strnum), .clk(clk), .ld(ldnum));  // open: sel, clr
  Subtractor #(.width(16)) subtractor_2 (
    .a(register_1_q), .b(register_2_q), .out(subtractor_2_out));  // open: bin, bout
  Comparator #(.width(16)) comparator_1 (.a(register_1_q), .b(register_2_q), .gt(comparator_1_gt), .eq(f), .lt(g));
  Subtractor #(.width(16)) subtractor_3 (
    .a(register_2_q), .b(register_1_q), .out(subtractor_3_out));  // open: bin, bout
  Adder adder_1 (.a(register_3_q), .b(8'h1), .out(adder_1_out));  // open: cin, cout
  Comparator comparator_2 (.a(register_3_q), .b(register_4_q), .gt(b), .eq(comparator_2_eq), .lt(comparator_2_lt));
  Comparator comparator_3 (.a(register_3_q), .b({8{1'b0}}), .gt(comparator_3_gt), .eq(c), .lt(comparator_3_lt));
  or or_1 (d, comparator_3_gt, comparator_3_lt);
  or or_2 (e, comparator_1_gt, g);
  or or_3 (h, f, comparator_1_gt);
  or or_4 (a, comparator_2_lt, comparator_2_eq);
endmodule
